# Fritzing sketch electrical-sketch (saved by Fritzing 0.9.6b)
perfboards: 1

parts:
  M1 = MKR ZERO
  U1 = MCP4725 [package=SOT23-6]
  U2 = Voltage Regulator - 5V [package="TO220 [THT]"]
  J1 = Power Jack [package=power_jack_pth]
  J2 = female pin header, 3 pins [form="♀ (female)"]
  J3 = female pin header, 2 pins [form="♀ (female)"]

nets:
  N1: M1.D0, J2.pin2
  N2: M1.D11_SDA, M1.SDA, U1.SDA
  N3: M1.D12_SCL, M1.SCL, U1.SCL
  GND: M1.GND, U1.VSS, U2.GND, J1.GND, J2.pin3, J3.pin1
  VCC: M1.VCC, U1.VDD
  N4: M1.VIN, U2.output_voltage, J2.pin1
  N5: U1.VOUT, J3.pin2
  N6: U2.input_voltage, J1.PWR

custom parts:
  MKR ZERO: arduino mrk zero SAMD21 Cortex-M0+ 32bit low power ARM MCU 256 meg flash 32kb sram 48mhz
